// Logisim project 3.2.circ as structural Verilog: 1 circuit, main circuit main
module main (
  input  [3:0] in_1,
  input  [3:0] in_2,
  input  [3:0] in_3,
  input  [3:0] in_4,
  input  suma_resta,
  input  C1_C2,
  output [3:0] out_7
);

  wire adder_1_cout;
  wire [3:0] adder_1_out, adder_2_out, adder_3_out, multiplexer_1_out, xor_1_out;

  assign xor_1_out = in_3 ^ in_4;  // XOR_Gate xor_1, 4 bits wide
  Adder #(.width(4)) adder_1 (.a(in_2), .b(in_3), .out(adder_1_out), .cout(adder_1_cout));  // open: cin
  Adder #(.width(4)) adder_2 (.a(in_2), .b(xor_1_out), .out(adder_2_out), .cin(1'b1));  // open: cout
  Multiplexer #(.width(4)) multiplexer_1 (
    .in0(adder_1_out), .in1(adder_2_out), .out(multiplexer_1_out), .sel(suma_resta));  // open: en
  Adder #(.width(4)) adder_3 (.a(in_1), .b(multiplexer_1_out), .out(adder_3_out), .cin(adder_1_cout));  // open: cout
  Multiplexer #(.width(4)) multiplexer_2 (
    .in0(adder_3_out), .in1(multiplexer_1_out), .out(out_7), .sel(C1_C2));  // open: en
endmodule
