// Logisim project 4boletin2.circ as structural Verilog: 1 circuit, main circuit main
module main (
  input  [3:0] A,
  input  [3:0] B,
  output out_3,
  output out_4,
  output out_5
);

  wire and_1_out, and_2_out, and_3_out, and_4_out, comparator_1_eq, comparator_1_gt, comparator_1_lt, igual;

  and and_1 (and_1_out, A[3], ~B[3]);  // AND_Gate
  and and_2 (and_2_out, ~A[3], B[3]);  // AND_Gate
  and and_3 (and_3_out, A[3], B[3]);
  or or_1 (igual, and_3_out, and_4_out);
  and and_4 (and_4_out, ~A[3], ~B[3]);  // AND_Gate
  Comparator #(.width(4)) comparator_1 (.a(A), .b(B), .gt(comparator_1_gt), .eq(comparator_1_eq), .lt(comparator_1_lt));
  Multiplexer multiplexer_1 (.in0(and_2_out), .in1(comparator_1_gt), .out(out_3), .sel(igual));  // open: en
  Multiplexer multiplexer_2 (.in0(and_1_out), .in1(comparator_1_lt), .out(out_5), .sel(igual));  // open: en
  and and_5 (out_4, igual, comparator_1_eq);
endmodule
