// Logisim project registro.circ as structural Verilog: 3 circuits, main circuit main
module main (
  input  in_1,
  input  \input ,
  input  clear,
  input  D1,
  input  D2,
  input  D3,
  input  D4,
  input  [1:0] Accionador,
  output out_9,
  output out_10,
  output out_11,
  output out_12
);

  wire multiplexer_1_out, multiplexer_2_out, multiplexer_3_out, multiplexer_4_out;

  Multiplexer #(.select(2)) multiplexer_1 (
    .in0(\input ), .in1(out_10), .in2(D1), .in3(out_9), .out(multiplexer_1_out), .sel(Accionador));  // open: en
  D_Flip_Flop d_ff_1 (.clk(in_1), .D(multiplexer_1_out), .Q(out_9), .reset(clear));  // open: Qn, preset, en
  D_Flip_Flop d_ff_2 (.clk(in_1), .D(multiplexer_2_out), .Q(out_10), .reset(clear));  // open: Qn, preset, en
  Multiplexer #(.select(2)) multiplexer_2 (
    .in0(out_9), .in1(out_11), .in2(D2), .in3(out_10), .out(multiplexer_2_out), .sel(Accionador));  // open: en
  Multiplexer #(.select(2)) multiplexer_3 (
    .in0(out_10), .in1(out_12), .in2(D3), .in3(out_11), .out(multiplexer_3_out), .sel(Accionador));  // open: en
  D_Flip_Flop d_ff_3 (.clk(in_1), .D(multiplexer_3_out), .Q(out_11), .reset(clear));  // open: Qn, preset, en
  Multiplexer #(.select(2)) multiplexer_4 (
    .in0(out_11), .in2(D4), .in3(out_12), .out(multiplexer_4_out), .sel(Accionador));  // open: in1, en
  D_Flip_Flop d_ff_4 (.clk(in_1), .D(multiplexer_4_out), .Q(out_12), .reset(clear));  // open: Qn, preset, en

  // Notes on the sheet:
  //   00 derecha
  //   01 Izquierda
  //   10 carga
  //   11 mantenimiento
endmodule

module Ej_3 (
);

  main main_1 ();  // open: input, clear, D2, D3, D4, Accionador, D1, in_1, out_9, out_10, out_11, out_12
endmodule

module w (
  input  in_1,
  input  \input ,
  input  clear,
  input  D1,
  input  D2,
  input  D3,
  input  D4,
  input  [1:0] Accionador
);

  wire d_ff_1_q, d_ff_2_q, d_ff_3_q, d_ff_4_q, multiplexer_1_out, multiplexer_2_out, multiplexer_3_out,
       multiplexer_4_out;

  Clock clock_1 ();  // open: out
  Multiplexer #(.select(2)) multiplexer_1 (
    .in0(\input ), .in1(d_ff_2_q), .in2(D1), .in3(d_ff_1_q), .out(multiplexer_1_out), .sel(Accionador));  // open: en
  D_Flip_Flop d_ff_1 (.clk(in_1), .D(multiplexer_1_out), .Q(d_ff_1_q), .reset(clear));  // open: Qn, preset, en
  D_Flip_Flop d_ff_2 (.clk(in_1), .D(multiplexer_2_out), .Q(d_ff_2_q), .reset(clear));  // open: Qn, preset, en
  Multiplexer #(.select(2)) multiplexer_2 (
    .in0(d_ff_1_q), .in1(d_ff_3_q), .in2(D2), .in3(d_ff_2_q), .out(multiplexer_2_out), .sel(Accionador));  // open: en
  Multiplexer #(.select(2)) multiplexer_3 (
    .in0(d_ff_2_q), .in1(d_ff_4_q), .in2(D3), .in3(d_ff_3_q), .out(multiplexer_3_out), .sel(Accionador));  // open: en
  D_Flip_Flop d_ff_3 (.clk(in_1), .D(multiplexer_3_out), .Q(d_ff_3_q), .reset(clear));  // open: Qn, preset, en
  Multiplexer #(.select(2)) multiplexer_4 (
    .in0(d_ff_3_q), .in2(D4), .in3(d_ff_4_q), .out(multiplexer_4_out), .sel(Accionador));  // open: in1, en
  D_Flip_Flop d_ff_4 (.clk(in_1), .D(multiplexer_4_out), .Q(d_ff_4_q), .reset(clear));  // open: Qn, preset, en

  // Notes on the sheet:
  //   00 derecha
  //   01 Izquierda
  //   10 carga
  //   11 mantenimiento
endmodule
