// Logisim project cosa.circ as structural Verilog: 1 circuit, main circuit main
module main (
  input  P,
  input  M,
  output s
);

  wire and_1_out, and_2_out, and_3_out, and_4_out, and_5_out, clock_1_out, not_1_out, not_2_out, or_1_out,
       or_2_out, Q0_q, Q0_qn, Q1_qn;

  Clock clock_1 (.out(clock_1_out));
  not not_1 (not_1_out, P);
  not not_2 (not_2_out, M);
  and and_1 (and_1_out, s, Q0_qn);
  and and_2 (and_2_out, s, P);
  and and_3 (and_3_out, Q1_qn, Q0_q, not_2_out);
  and and_4 (and_4_out, Q1_qn, M);
  and and_5 (and_5_out, s, P);
  or or_1 (or_1_out, and_1_out, and_2_out, and_3_out);
  or or_2 (or_2_out, and_4_out, and_5_out);
  D_Flip_Flop Q1 (.clk(clock_1_out), .D(or_1_out), .Q(s), .Qn(Q1_qn));  // open: preset, en, reset
  D_Flip_Flop Q0 (.clk(clock_1_out), .D(or_2_out), .Q(Q0_q), .Qn(Q0_qn));  // open: preset, en, reset

  // Notes on the sheet:
  //   e1
  //   CLK
  //   ¬e1
  //   ¬e0
  //   e0
  //   Q1
  //   ¬Q1
  //   Q0
  //   ¬Q0
endmodule
