// Logisim project 3.2.circ as structural Verilog: 1 circuit, main circuit main
module main (
  input  [3:0] in_1,
  input  [3:0] in_2,
  input  [3:0] in_3,
  input  in_4,
  input  C1_C2,
  output out_6,
  output [3:0] out_7
);

  wire and_1_out, and_2_out;
  wire [3:0] adder_1_out, xor_1_out;

  Adder #(.width(4)) adder_1 (.a(in_1), .b(xor_1_out), .out(adder_1_out), .cin(and_1_out), .cout(out_6));
  assign xor_1_out = {4{in_4}} ^ in_3;  // XOR_Gate xor_1, 4 bits wide
  and and_1 (and_1_out, C1_C2, in_4);
  and and_2 (and_2_out, out_6, ~C1_C2);  // AND_Gate
  Adder #(.width(4)) adder_2 (.a(adder_1_out), .b(in_2), .out(out_7), .cin(and_2_out));  // open: cout
endmodule
