// Logisim project Ej3.circ as structural Verilog: 1 circuit, main circuit main
module main (
  input  [3:0] in_1,
  input  [3:0] in_2,
  input  in_3,
  input  in_4,
  output [3:0] out_5,
  output out_6,
  output out_7,
  output out_8
);

  wire [3:0] adder_2_out, adder_3_out, RESSUM;

  Adder #(.width(4)) adder_1 (.a(in_1), .b(in_2), .out(RESSUM), .cin(1'b1), .cout(out_8));
  Multiplexer #(.width(4)) multiplexer_1 (.in0(RESSUM), .sel(in_3));  // open: in1, out, en
  Adder #(.width(4)) adder_2 (.a(in_1), .b(in_2), .out(adder_2_out), .cout(out_6));  // open: cin
  Adder #(.width(4)) adder_3 (.a(in_1), .b(in_2), .out(adder_3_out), .cin(1'b1), .cout(out_7));
  Multiplexer multiplexer_2 (.sel(in_4));  // open: in0, in1, out, en

  // Other names for the same wires on the sheet: Res[3:0] = in_1; SUM[3:0] = in_1; Res2[3:0] = in_2; SUM2[3:0] = in_2
endmodule
